# Fritzing sketch Final_Project_Schematic_L298N (saved by Fritzing 0.9.4)
breadboards: 2

parts:
  BAT1 = BC9VPC [package=bc9vpc]
  Part2 = InvenSense MPU6050
  Part5 = Bluetooth HC-05 Macho
  M2 = DC Motor
  M3 = DC Motor
  R1 = Resistor [tolerance=±5% resistance=1k package=THT]
  R2 = Resistor [tolerance=±5% resistance=2.2k package=THT]
  HC-SR04_Sensor_1 = HC-SR04 Ultrasonic Distance Sensor
  HC-SR04_Sensor_2 = HC-SR04 Ultrasonic Distance Sensor
  S1 = H-Bridge with L298N
  Part6 = Arduino Uno (Rev3)
  R3 = Resistor [tolerance=±5% resistance=220 package=THT]
  LED1 = LED - 5mm [color="Blue (470nm)" package="5 mm [THT]"]
  VCC1 = Battery block 9V

nets (from the breadboard view):
  N1: BAT1.V+, Part6.VIN
  GND: BAT1.V-, Part2.GND, Part5.GND, R2.Pin_0, HC-SR04_Sensor_1.GND, HC-SR04_Sensor_2.GND, S1.GND, Part6.GND, LED1.cathode, VCC1.-
  VCC: Part2.VCC, Part5.VCC, HC-SR04_Sensor_1.VCC, HC-SR04_Sensor_2.VCC, Part6.3V3
  N2: Part2.SCL, Part6.A5/SCL
  N3: Part2.SDA, Part6.A4/SDA
  N4: Part2.INT, Part6.D2
  N5: Part5.TXD, Part6.D0/RX
  N6: Part5.RXD, R1.Pin_0, R2.Pin_1
  N7: M2.pin_1, S1.M1-02
  N8: M2.pin_2, S1.M1-01
  N9: M3.pin_1, S1.M2-01
  N10: M3.pin_2, S1.M2-02
  N11: R1.Pin_1, Part6.D1/TX
  N12: HC-SR04_Sensor_1.TRIG, Part6.D13/SCK
  N13: HC-SR04_Sensor_1.ECHO, Part6.D12/MISO
  N14: HC-SR04_Sensor_2.TRIG, Part6.D11_PWM/MOSI
  N15: HC-SR04_Sensor_2.ECHO, Part6.D10_PWM/SS
  N16: S1.12V, VCC1.+
  N17: S1.ENA, Part6.D5_PWM
  N18: S1.IN1, Part6.D3_PWM
  N19: S1.IN2, Part6.D4
  N20: S1.IN3, Part6.D8
  N21: S1.IN4, Part6.D6_PWM
  N22: S1.ENB, Part6.D7
  N23: Part6.D9_PWM, R3.Pin_1
  N24: R3.Pin_0, LED1.anode

custom parts:
  H-Bridge with L298N: h-bridge
